// Logisim project hw3.circ as structural Verilog: 3 circuits, main circuit carry
module carry (
  input  in_1,
  input  in_2,
  input  in_3,
  output out_4,
  output out_5
);

  wire and_2_out, or_1_out, or_2_out, xor_1_out;

  and and_1 (out_4, or_1_out, or_2_out);
  or or_1 (or_1_out, in_1, in_2);
  and and_2 (and_2_out, in_1, in_2);
  or or_2 (or_2_out, and_2_out, in_3);
  xor xor_1 (xor_1_out, in_1, in_2);
  xor xor_2 (out_5, in_3, xor_1_out);
endmodule

module adder (
  input  in_1,
  input  in_2,
  input  in_3,
  input  in_4,
  input  in_5,
  input  in_6,
  input  in_7,
  input  in_8,
  input  in_9,
  output out_10,
  output out_11,
  output out_12,
  output out_13,
  output out_14,
  output out_15
);

  wire carry_2_out_4, carry_3_out_4, carry_4_out_4, undriven;

  carry carry_1 (.out_4(out_11), .in_1(undriven), .in_2(in_2), .out_5(out_12), .in_3(carry_2_out_4));
  carry carry_2 (.out_4(carry_2_out_4), .in_1(in_3), .in_2(in_6), .out_5(out_13), .in_3(carry_3_out_4));
  carry carry_3 (.out_4(carry_3_out_4), .in_1(in_4), .in_2(in_4), .out_5(out_14), .in_3(carry_4_out_4));
  carry carry_4 (.out_4(carry_4_out_4), .in_1(in_8), .in_2(in_5), .out_5(out_15), .in_3(in_9));

  assign in_7 = in_4;
  assign out_10 = in_1;
endmodule

module alu (
  input  [3:0] in_1,
  input  [3:0] in_2,
  input  [2:0] in_3,
  input  in_4,
  output out_5,
  output [3:0] out_6,
  output [3:0] out_7
);

  wire [3:0] undriven;

  // adder adder_1: pin names not known; wires that end beside it: out_5, out_7, in_1, in_2, in_4
  Multiplexer #(.select(3), .width(4), .disabled(0), .enable("false")) multiplexer_1 (
    .in0(undriven), .out(out_6), .sel(in_3));  // open: in1, in2, in3, in4, in5, in6, in7
endmodule
